# Fritzing sketch circuit (saved by Fritzing 0.9.0b)
breadboards: 1

parts:
  Part1 = Arduino Mega 2560 (Rev3)
  Part2 = Logic Level Converter
  PIR1 = PIR sensor
  U1 = ESP8266 WiFi Module [part_number=ESP8266]

nets:
  N1: Part1.D19/RX1, Part2.TX2_HV
  N2: Part1.D18/TX1, Part2.RX2_HV
  GND: Part1.GND, Part2.GND, PIR1.GND, U1.GND
  3V3: Part1.3V3, Part2.LV, U1.VCC, U1.RST, U1.CH_PD
  5V: Part1.5V, Part2.HV, PIR1.VDD
  N3: Part1.D2_PWM, PIR1.SIG
  N4: Part2.TX2_LV, U1.TXD
  N5: Part2.RX2_LV, U1.RXD

custom parts:
  ESP8266 WiFi Module: Generic WiFi Module based on the ESP8266 with onboard PCB antenna and UART communications
